# Fritzing sketch PULSE SENSOR (saved by Fritzing 0.9.3b)
circuit board: 5.32982cm x 3.20259cm
breadboards: 1

parts:
  Raspberry_Pi1 = Raspberry Pi B+
  ADC1 = MCP3008 [package=dil16]

nets:
  3V3: Raspberry_Pi1.3v3, Raspberry_Pi1.3V3, ADC1.VREF, ADC1.VDD
  N1: Raspberry_Pi1.GND, ADC1.DGND, ADC1.AGND
  N2: Raspberry_Pi1.GPIO10, ADC1.Din
  N3: Raspberry_Pi1.GPIO9, ADC1.Dout
  N4: Raspberry_Pi1.GPIO11, ADC1.CLK
  N5: Raspberry_Pi1.GPIO8, ADC1.CS/SHDN

notes:
  Baltej Bal
  MCP3008
  Data Cable
